// Logisim project ALU.circ as structural Verilog: 13 circuits, main circuit main
module main (
  input  [15:0] A,
  input  [15:0] B,
  input  sub,
  input  [2:0] select,
  input  reset,
  output greater_than,
  output equal,
  output less_than,
  output [15:0] result,
  output overflow
);

  wire not_1_out, overflow_1_overflow;
  wire [15:0] mux_1_result;

  MUX mux_1 (
    .A(A), .B(B), .result(mux_1_result), .select(select), .greater_than(greater_than), .equal(equal),
    .less_than(less_than));
  reset reset_1 (.result(mux_1_result), .reset(reset), .\output (result));
  overflow overflow_1 (.sub(sub), .A(A), .B(B), .result(mux_1_result), .overflow(overflow_1_overflow));
  not not_1 (not_1_out, reset);
  and and_1 (overflow, overflow_1_overflow, not_1_out);
endmodule

module _16_bit_adder (
  input  [15:0] A,
  input  [15:0] B,
  input  cin,
  output [15:0] Sum,
  output Cout,
  output C15
);

  wire n1_bit_adder_1_cout, n1_bit_adder_2_cout, n1_bit_adder_3_cout, n1_bit_adder_4_cout,
       n1_bit_adder_5_cout, n1_bit_adder_6_cout, n1_bit_adder_7_cout, n1_bit_adder_8_cout,
       n1_bit_adder_9_cout, n1_bit_adder_10_cout, n1_bit_adder_11_cout, n1_bit_adder_12_cout,
       n1_bit_adder_13_cout, n1_bit_adder_15_cout;

  _1_bit_adder u_1_bit_adder_1 (.A(A[0]), .B(B[0]), .Cin(cin), .Sum(Sum[0]), .Cout(n1_bit_adder_1_cout));
  _1_bit_adder u_1_bit_adder_2 (
    .A(A[8]), .B(B[8]), .Cin(n1_bit_adder_15_cout), .Sum(Sum[8]), .Cout(n1_bit_adder_2_cout));
  _1_bit_adder u_1_bit_adder_3 (
    .A(A[1]), .B(B[1]), .Cin(n1_bit_adder_1_cout), .Sum(Sum[1]), .Cout(n1_bit_adder_3_cout));
  _1_bit_adder u_1_bit_adder_4 (
    .A(A[9]), .B(B[9]), .Cin(n1_bit_adder_2_cout), .Sum(Sum[9]), .Cout(n1_bit_adder_4_cout));
  _1_bit_adder u_1_bit_adder_5 (
    .A(A[2]), .B(B[2]), .Cin(n1_bit_adder_3_cout), .Sum(Sum[2]), .Cout(n1_bit_adder_5_cout));
  _1_bit_adder u_1_bit_adder_6 (
    .A(A[10]), .B(B[10]), .Cin(n1_bit_adder_4_cout), .Sum(Sum[10]), .Cout(n1_bit_adder_6_cout));
  _1_bit_adder u_1_bit_adder_7 (
    .A(A[11]), .B(B[11]), .Cin(n1_bit_adder_6_cout), .Sum(Sum[11]), .Cout(n1_bit_adder_7_cout));
  _1_bit_adder u_1_bit_adder_8 (
    .A(A[3]), .B(B[3]), .Cin(n1_bit_adder_5_cout), .Sum(Sum[3]), .Cout(n1_bit_adder_8_cout));
  _1_bit_adder u_1_bit_adder_9 (
    .A(A[4]), .B(B[4]), .Cin(n1_bit_adder_8_cout), .Sum(Sum[4]), .Cout(n1_bit_adder_9_cout));
  _1_bit_adder u_1_bit_adder_10 (
    .A(A[12]), .B(B[12]), .Cin(n1_bit_adder_7_cout), .Sum(Sum[12]), .Cout(n1_bit_adder_10_cout));
  _1_bit_adder u_1_bit_adder_11 (
    .A(A[13]), .B(B[13]), .Cin(n1_bit_adder_10_cout), .Sum(Sum[13]), .Cout(n1_bit_adder_11_cout));
  _1_bit_adder u_1_bit_adder_12 (
    .A(A[5]), .B(B[5]), .Cin(n1_bit_adder_9_cout), .Sum(Sum[5]), .Cout(n1_bit_adder_12_cout));
  _1_bit_adder u_1_bit_adder_13 (
    .A(A[6]), .B(B[6]), .Cin(n1_bit_adder_12_cout), .Sum(Sum[6]), .Cout(n1_bit_adder_13_cout));
  _1_bit_adder u_1_bit_adder_14 (.A(A[14]), .B(B[14]), .Cin(n1_bit_adder_11_cout), .Sum(Sum[14]), .Cout(C15));
  _1_bit_adder u_1_bit_adder_15 (
    .A(A[7]), .B(B[7]), .Cin(n1_bit_adder_13_cout), .Sum(Sum[7]), .Cout(n1_bit_adder_15_cout));
  _1_bit_adder u_1_bit_adder_16 (.A(A[15]), .B(B[15]), .Cin(C15), .Sum(Sum[15]), .Cout(Cout));
endmodule

module _1_bit_adder (
  input  A,
  input  B,
  input  Cin,
  output Sum,
  output Cout
);

  wire and_1_out, and_2_out, xor_1_out;

  xor xor_1 (xor_1_out, A, B);
  and and_1 (and_1_out, Cin, xor_1_out);
  and and_2 (and_2_out, A, B);
  xor xor_2 (Sum, xor_1_out, Cin);
  or or_1 (Cout, and_1_out, and_2_out);
endmodule

module _16_bit_subtractor (
  input  [15:0] A,
  input  [15:0] B,
  output [15:0] Subtraction,
  output Borrow_out
);

  wire n16_bit_adder_1_cout;
  wire [15:0] not_1_out;

  not not_1 (not_1_out[0], B[0]);
  not not_2 (not_1_out[1], B[1]);
  not not_3 (not_1_out[2], B[2]);
  not not_4 (not_1_out[3], B[3]);
  not not_5 (not_1_out[4], B[4]);
  not not_6 (not_1_out[5], B[5]);
  not not_7 (not_1_out[6], B[6]);
  not not_8 (not_1_out[7], B[7]);
  not not_9 (not_1_out[8], B[8]);
  not not_10 (not_1_out[9], B[9]);
  not not_11 (not_1_out[10], B[10]);
  not not_12 (not_1_out[11], B[11]);
  not not_13 (not_1_out[12], B[12]);
  not not_14 (not_1_out[13], B[13]);
  not not_15 (not_1_out[14], B[14]);
  not not_16 (not_1_out[15], B[15]);
  _16_bit_adder u_16_bit_adder_1 (
    .A(A), .B(not_1_out), .cin(1'b1), .Sum(Subtraction), .Cout(n16_bit_adder_1_cout));  // open: C15
  not not_17 (Borrow_out, n16_bit_adder_1_cout);
endmodule

module AND (
  input  [15:0] A,
  input  [15:0] B,
  output [15:0] AND_result
);

  assign AND_result = A & B;  // AND_Gate and_1, 16 bits wide
endmodule

module or_gate (
  input  [15:0] A,
  input  [15:0] B,
  output [15:0] OR_result
);

  assign OR_result = A | B;  // OR_Gate or_1, 16 bits wide
endmodule

module XOR (
  input  [15:0] cin,
  input  [15:0] cin_2,
  output [15:0] OR_result
);

  assign OR_result = cin ^ cin_2;  // XOR_Gate xor_1, 16 bits wide
endmodule

module NOT (
  input  [15:0] cin,
  output [15:0] NOT_result
);

  assign NOT_result = ~cin;  // NOT_Gate not_1, 16 bits wide
endmodule

module increment (
  input  [15:0] A,
  output [15:0] result,
  output cout
);

  _16_bit_adder u_16_bit_adder_1 (.A(A), .B(16'h1), .cin(1'b0), .Sum(result), .Cout(cout));  // open: C15
endmodule

module MUX (
  input  [15:0] A,
  input  [15:0] B,
  input  [2:0] select,
  output [15:0] result,
  output equal,
  output greater_than,
  output less_than
);

  wire [15:0] and_1_and_result, increment_1_result, n16_bit_adder_1_sum, n16_bit_comparator_1_result,
       n16_bit_subtractor_1_subtraction, not_1_not_result, or_gate_1_or_result, xor_1_or_result;

  AND and_1 (.A(A), .B(B), .AND_result(and_1_and_result));
  _16_bit_comparator u_16_bit_comparator_1 (
    .A(A), .B(B), .equal(equal), .result(n16_bit_comparator_1_result), .greater_than(greater_than),
    .less_than(less_than));
  _16_bit_adder u_16_bit_adder_1 (.A(A), .B(B), .cin(1'b0), .Sum(n16_bit_adder_1_sum));  // open: Cout, C15
  _16_bit_subtractor u_16_bit_subtractor_1 (
    .A(A), .B(B), .Subtraction(n16_bit_subtractor_1_subtraction));  // open: Borrow_out
  or_gate or_gate_1 (.A(A), .B(B), .OR_result(or_gate_1_or_result));
  NOT not_1 (.cin(A), .NOT_result(not_1_not_result));
  XOR xor_1 (.cin(A), .cin_2(B), .OR_result(xor_1_or_result));
  increment increment_1 (.A(A), .result(increment_1_result));  // open: cout
  Multiplexer #(.select(3), .width(16)) multiplexer_1 (
    .in0(n16_bit_adder_1_sum), .in1(n16_bit_subtractor_1_subtraction), .in2(and_1_and_result),
    .in3(or_gate_1_or_result), .in4(not_1_not_result), .in5(xor_1_or_result), .in6(increment_1_result),
    .in7(n16_bit_comparator_1_result), .out(result), .sel(select));  // open: en
endmodule

module reset (
  input  [15:0] result,
  input  reset,
  output [15:0] \output 
);

  Multiplexer #(.width(16)) multiplexer_1 (.in0(result), .in1({16{1'b0}}), .out(\output ), .sel(reset));  // open: en
endmodule

module overflow (
  input  sub,
  input  [15:0] A,
  input  [15:0] B,
  input  [15:0] result,
  output overflow
);

  wire and_1_out, and_2_out, and_3_out, and_4_out, not_1_out, not_2_out, xor_1_out, xor_2_out, xor_3_out;

  xor xor_1 (xor_1_out, A[15], B[15]);
  xor xor_2 (xor_2_out, A[15], result[15]);
  not not_1 (not_1_out, sub);
  not not_2 (not_2_out, xor_1_out);
  and and_1 (and_1_out, not_2_out, xor_2_out);
  xor xor_3 (xor_3_out, A[15], B[15]);
  and and_2 (and_2_out, xor_2_out, xor_3_out);
  and and_3 (and_3_out, not_1_out, and_1_out);
  and and_4 (and_4_out, sub, and_2_out);
  or or_1 (overflow, and_3_out, and_4_out);
endmodule

module _16_bit_comparator (
  input  [15:0] A,
  input  [15:0] B,
  output equal,
  output [15:0] result,
  output greater_than,
  output less_than
);

  wire n16_bit_subtractor_1_borrow_out, not_1_out, or_1_out;
  wire [15:0] n16_bit_subtractor_1_subtraction;

  _16_bit_subtractor u_16_bit_subtractor_1 (
    .A(A), .B(B), .Subtraction(n16_bit_subtractor_1_subtraction), .Borrow_out(n16_bit_subtractor_1_borrow_out));
  not not_1 (not_1_out, equal);
  and and_1 (less_than, n16_bit_subtractor_1_borrow_out, not_1_out);
  not not_2 (greater_than, or_1_out);
  or or_1 (or_1_out, equal, less_than);
  nor nor_1 (equal, n16_bit_subtractor_1_subtraction[0], n16_bit_subtractor_1_subtraction[1], n16_bit_subtractor_1_subtraction[2], n16_bit_subtractor_1_subtraction[3], n16_bit_subtractor_1_subtraction[4], n16_bit_subtractor_1_subtraction[5], n16_bit_subtractor_1_subtraction[6], n16_bit_subtractor_1_subtraction[7], n16_bit_subtractor_1_subtraction[8], n16_bit_subtractor_1_subtraction[9], n16_bit_subtractor_1_subtraction[10], n16_bit_subtractor_1_subtraction[11], n16_bit_subtractor_1_subtraction[12], n16_bit_subtractor_1_subtraction[13], n16_bit_subtractor_1_subtraction[14], n16_bit_subtractor_1_subtraction[15]);

  assign result = {{13{1'b0}}, greater_than, less_than, equal};
endmodule
